# Fritzing sketch circuit (saved by Fritzing 0.9.3b)
circuit board: 5.23783cm x 4.08766cm

parts:
  IC3 = IC, DIP package, 28 pins [chip_label=ATmega328P]
  XTAL1 = Crystal [frequency="16 Mhz" package=THT]
  R9 = Resistor [tolerance=±5% resistance=91 package=THT]
  R10 = Resistor [tolerance=±5% resistance=91 package=THT]
  C2 = Ceramic Capacitor [capacitance=100nF package="200 mil [THT, multilayer]"]
  C1 = Ceramic Capacitor [capacitance=100nF package="200 mil [THT, multilayer]"]
  J3 = rounded female pin header, 1 pin [form="♀ (female rounded)"]
  RS485_Power = rounded female pin header, 2 pins [form="♀ (female rounded)"]
  R12 = Resistor [tolerance=±5% resistance=1.5k package=THT]
  CONN1 = USB connector [package=THT]
  RS485_Tx = rounded female pin header, 1 pin [form="♀ (female rounded)"]
  R13 = Resistor [tolerance=±5% resistance=100 package=THT]
  LED1 = LED - 5mm [color="Green (565nm)" package="5 mm [THT]"]
  LED2 = LED - 5mm [color="Yellow (595nm)" package="5 mm [THT]"]
  D4 = Zener Diode [part_number=1N4732A breakdown_voltage=3.6V package="200 mil [THT]"]
  D3 = Zener Diode [part_number=1N4732A breakdown_voltage=3.6V package="200 mil [THT]"]
  R14 = Resistor [tolerance=±5% resistance=100 package=THT]

nets:
  N1: IC3.pin1, J3.pin1
  Tx: IC3.pin3, RS485_Tx.pin1
  N2: IC3.pin4, R9.Pin_0
  LED gr: IC3.pin5, R13.Pin_0
  LED y: IC3.pin6, LED2.anode
  5V: IC3.pin7, IC3.pin20, RS485_Power.pin1, R12.Pin_0, CONN1.5V
  GND: IC3.pin8, C2.0, C1.0, RS485_Power.pin2, CONN1.GND, CONN1.chassis5, CONN1.chassis6, LED1.cathode, D4.anode, D3.anode, R14.Pin_0
  N3: IC3.pin9, XTAL1.pin_0, C1.1
  N4: IC3.pin10, XTAL1.pin_1, C2.1
  N5: IC3.pin13, R10.Pin_0
  Row5: IC3.pin14
  USB D+: R9.Pin_1, CONN1.d+, D3.cathode
  USB D-: R10.Pin_1, R12.Pin_1, CONN1.d-, D4.cathode
  N6: R13.Pin_1, LED1.anode
  N7: LED2.cathode, R14.Pin_1

custom parts:
  Zener Diode: A standard asdf zener diode
